# Fritzing sketch Untitled Sketch 2 (saved by Fritzing 0.9.3b)
breadboards: 1

parts:
  元件1 = Arduino BT
  hc-sr1 = hc-sr04
  LED1 = LED - 5mm [color="Red (633nm)" package="5 mm [THT]"]  # not connected

nets:
  GND: 元件1.GND, hc-sr1.GND
  N1: 元件1.D2, hc-sr1.Trig
  N2: 元件1.PWM_D3, hc-sr1.Echo
  5V: 元件1.5V, hc-sr1.VCC
